# Fritzing sketch TMC2130-sample-circuit  (saved by Fritzing 0.9.3b)
breadboards: 1

parts:
  SilentStepStick_TMC1 = SilentStepStick TMC2130 [package=SO16]
  Part1 = Arduino Mega ADK (Rev3)
  M1 = Stepper Motor - Bipolar
  Power_plug1 = Power plug

nets:
  N1: SilentStepStick_TMC1.SDO, Part1.D50/MISO
  N2: SilentStepStick_TMC1.CS, Part1.D12_PWM
  N3: SilentStepStick_TMC1.SCK, Part1.D52/SCK
  N4: SilentStepStick_TMC1.SDI, Part1.D51/MOSI
  N5: SilentStepStick_TMC1.STEP, Part1.D11_PWM
  N6: SilentStepStick_TMC1.DIR, Part1.D10_PWM
  N7: SilentStepStick_TMC1.GND#8, Part1.GND
  N8: SilentStepStick_TMC1.VIO, Part1.5V
  N9: SilentStepStick_TMC1.1B, M1.D
  N10: SilentStepStick_TMC1.1A, M1.B
  N11: SilentStepStick_TMC1.2A, M1.C
  N12: SilentStepStick_TMC1.2B, M1.A
  N13: SilentStepStick_TMC1.GND#14, Power_plug1.GND
  N14: SilentStepStick_TMC1.VMOT, Power_plug1.VCC

custom parts:
  SilentStepStick TMC2130: The TMC2130 provides an integrated motor driver solution for 3D-Printing, Cameras, Scanners and other automated equipment applications. The device has an integrated microstepping indexer, the sensorless stall detection technology StallGuard2™, the sensorless load dependent current control CoolStep™ and the completely noiseless current control mode StealthChop™ and is intended to drive a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
